# Fritzing sketch ControlBoard_Basic_x8_v1.0 (saved by Fritzing 1.0.5)
circuit board: 7.2cm x 12.5cm
breadboards: 1

parts:
  Wiz5500_Ethernet_Co-Processor = Adafruit Wiz5500 Ethernet Co-Processor Breakout Board [part_number=#6348]
  KB2040 = Adafruit KB2040
  J1 = RJ11 Jack [package=rj11-6]
  J2 = RJ11 Jack [package=rj11-6]
  J3 = RJ11 Jack [package=rj11-6]
  J4 = RJ11 Jack [package=rj11-6]
  J5 = RJ11 Jack [package=rj11-6]
  J6 = RJ11 Jack [package=rj11-6]
  J7 = RJ11 Jack [package=rj11-6]
  J8 = RJ11 Jack [package=rj11-6]
  MCP23017 = MCP23017 I2C I/O Expander
  R1 = Resistor [tolerance=±5% power=0.25W resistance=4.7k package=THT]
  R2 = Resistor [tolerance=±5% power=0.25W resistance=4.7k package=THT]
  J9 = screw terminal, 10 pins

nets:
  3.3v: Wiz5500_Ethernet_Co-Processor.VIN, KB2040.3.3V, MCP23017.VDD, MCP23017.RESET, R1.Pin_0, R2.Pin_0
  gnd: Wiz5500_Ethernet_Co-Processor.GND, KB2040.GND, J1.4, J2.4, J3.4, J4.4, J5.4, J6.4, J7.4, J8.4, MCP23017.VSS, MCP23017.A0, MCP23017.A1, MCP23017.A2, J9.pin10
  N1: Wiz5500_Ethernet_Co-Processor.SCK, KB2040.SCLK
  N2: Wiz5500_Ethernet_Co-Processor.MISO_MCU, KB2040.MISO
  N3: Wiz5500_Ethernet_Co-Processor.MOSI, KB2040.MOSI
  N4: Wiz5500_Ethernet_Co-Processor.CS, KB2040.D10
  N5: Wiz5500_Ethernet_Co-Processor.RST, KB2040.A2
  raw: KB2040.RAW, J1.2, J2.2, J3.2, J4.2, J5.2, J6.2, J7.2, J8.2, J9.pin9
  N6: KB2040.D0, MCP23017.SDA, R2.Pin_1
  N7: KB2040.D1, MCP23017.SCL, R1.Pin_1
  N8: KB2040.D2, J1.3
  N9: KB2040.D3, J2.3
  N10: KB2040.D4, J3.3
  N11: KB2040.D5, J4.3
  N12: KB2040.D6, J8.3
  N13: KB2040.D7, J7.3
  N14: KB2040.D8, J6.3
  N15: KB2040.D9, J5.3
  N16: J1.5, MCP23017.GPB0
  N17: J2.5, MCP23017.GPB1
  N18: J3.5, MCP23017.GPB2
  N19: J4.5, MCP23017.GPB3
  N20: J5.5, MCP23017.GPB4
  N21: J6.5, MCP23017.GPB5
  N22: J7.5, MCP23017.GPB6
  N23: J8.5, MCP23017.GPB7
  N24: MCP23017.GPA0, J9.pin8
  N25: MCP23017.GPA1, J9.pin7
  N26: MCP23017.GPA2, J9.pin6
  N27: MCP23017.GPA3, J9.pin5
  N28: MCP23017.GPA4, J9.pin4
  N29: MCP23017.GPA5, J9.pin3
  N30: MCP23017.GPA6, J9.pin2
  N31: MCP23017.GPA7, J9.pin1

notes:
  OSC RemoteIO v1.0
  Designed By: Luthien Finch
  https://github.com/TheLadyLuthien/OSC_RemoteIO

custom parts:
  Adafruit Wiz5500 Ethernet Co-Processor Breakout Board: Wireless is wonderful, but sometimes you want the strong reliability of a wire. If you want to incorporate an Ethernet port as a great addition to your IoT project, this Wiz5500 Ethernet Breakout will let you add quick and easy wired Internet. Just plug in a standard Ethernet cable, and run the Ethernet Arduino library (or CircuitPython) for cross-platform networking. Ethernet is a tried-and-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
  MCP23017 I2C I/O Expander: The MCP23017 uses two i2c pins (these can be shared with other i2c devices), and in exchange gives you 16 general purpose pins. You can set each of 16 pins to be input, output, input with a pullup or open drain. There's even the ability to get an interrupt via an external pin when any of the inputs change so you don't have to keep polling the chip.
